// Logisim project battleship.circ as structural Verilog: 2 circuits, main circuit main
module main (
  input  [3:0] PosicaoTiro,
  input  [3:0] Navio1,
  input  [3:0] Navio2,
  output Acertou,
  output Errou
);

  wire button_1_out, comparator_1_eq, comparator_2_eq, or_1_out;
  wire [3:0] Disparador_out_2, encoder_1_out_2, encoder_2_out_2;

  Encoder Disparador (.Navio(PosicaoTiro), .out_2(Disparador_out_2));
  Encoder encoder_1 (.Navio(Navio1), .out_2(encoder_1_out_2));
  Encoder encoder_2 (.Navio(Navio2), .out_2(encoder_2_out_2));
  Comparator #(.width(4)) comparator_1 (
    .a(encoder_1_out_2), .b(Disparador_out_2), .eq(comparator_1_eq));  // open: gt, lt
  Comparator #(.width(4)) comparator_2 (
    .a(Disparador_out_2), .b(encoder_2_out_2), .eq(comparator_2_eq));  // open: gt, lt
  Button #(.press("passive")) button_1 (.out(button_1_out));
  or or_1 (or_1_out, comparator_1_eq, comparator_2_eq);
  and and_1 (Acertou, or_1_out, button_1_out);
  buf and_2 (Errou, ~button_1_out);  // AND_Gate AND_Gate
endmodule

module Encoder (
  input  [3:0] Navio,
  output [3:0] out_2
);

  wire and_3_out, and_4_out, and_5_out, and_6_out, and_7_out, and_8_out, not_1_out, not_2_out, not_3_out,
       not_4_out;

  not not_1 (not_1_out, Navio[3]);
  not not_2 (not_2_out, Navio[2]);
  not not_3 (not_3_out, Navio[1]);
  not not_4 (not_4_out, Navio[0]);
  and and_1 (out_2[0], Navio[3], Navio[2], not_3_out, not_4_out);
  and and_2 (out_2[1], Navio[3], Navio[1], Navio[0]);
  and and_3 (and_3_out, not_1_out, not_2_out, not_4_out);
  and and_4 (and_4_out, not_1_out, Navio[2], Navio[0]);
  and and_5 (and_5_out, not_1_out, not_2_out, Navio[0]);
  and and_6 (and_6_out, not_1_out, Navio[2], not_4_out);
  and and_7 (and_7_out, Navio[3], not_3_out, Navio[0]);
  and and_8 (and_8_out, Navio[3], Navio[1], not_4_out);
  or or_1 (out_2[2], and_3_out, and_4_out);
  or or_2 (out_2[3], and_5_out, and_6_out, and_7_out, and_8_out);
endmodule
